# Fritzing sketch schematic (saved by Fritzing 0.9.3b)
circuit board: 20.9247cm x 11.7674cm
breadboards: 1

parts:
  PART2 = Sound Detector
  C1 = Electrolytic Capacitor [capacitance=1µF package="100 mil [THT, electrolytic]"]
  RGB_SMD_LED1 = SMD RGB LED (WS2812) [package=5050]
  Part1 = Arduino Uno (Rev3)
  S1 = Pushbutton [package="[THT]"]
  R1 = Resistor [tolerance=±5% resistance=220 package="0603 [SMD]"]
  C2 = Electrolytic Capacitor [capacitance=1µF package="100 mil [THT, electrolytic]"]
  BAT1 = BC9VPC [package=bc9vpc]

nets:
  N1: PART2.ENVELOPE, R1.Pin_0
  VCC: PART2.VCC, C1.+, Part1.5V, C2.+
  GND: PART2.GND, C1.-, RGB_SMD_LED1.VSS, Part1.GND, S1.Pin_3, S1.Pin_4, C2.-, BAT1.V-
  N2: RGB_SMD_LED1.DIn, Part1.D6_PWM
  N3: RGB_SMD_LED1.VCC, BAT1.V+
  N4: Part1.A0, R1.Pin_1
  N5: Part1.D12/MISO, S1.Pin_1, S1.Pin_2

notes:
  A 9V battery is not used. It is a placeholder for a 5V, 3A micro USB charging module, powered by a charger with the same specifications
  The sound module is a Sparkfun Sound Detector
  The LED shown is one LED in a RGB LED strip
  Expected Behaviour:
  The project will start with a delay of 5 seconds to calibrate the room noise level. Then the user can push a button to activate the first animation. Choosing colours on the processing sketch will determine what colour is show on the LED. The buttons need to be double clicked to be activated. So when selecting colours, double click a square, then pick the colour, double click it again to confirm and then click on the next square or submit button. The colours that are transmitted are printed in the Debugger.
  The first two animations are the same, but can have different colours. The third animation will not move, but show the graident between colours.

custom parts:
  Sound Detector: Electret microphone with multiple outputs. - First output is the actual audio - Second output is the amplitude envelope - Third output is a binary "sound present" indication - high while sound is present, low otherwise. Visit sparkfun.com for more documentations.
